# Fritzing sketch db19-idc20-adapter (saved by Fritzing 1.0.1rc)
circuit board: 1.80915cm x 3.33989cm
breadboards: 1

parts:
  Pad29 = Pad [width=3 height=2 connect=center]
  Pad30 = Pad [width=3 height=2 connect=center]
  Pad31 = Pad [width=3 height=2 connect=center]
  Pad32 = Pad [width=3 height=2 connect=center]
  Pad33 = Pad [width=3 height=2 connect=center]
  Pad34 = Pad [width=3 height=2 connect=center]
  Pad35 = Pad [width=3 height=2 connect=center]
  Pad36 = Pad [width=3 height=2 connect=center]
  Pad37 = Pad [width=3 height=2 connect=center]
  Pad38 = Pad [width=3 height=2 connect=center]
  Pad39 = Pad [width=3 height=2 connect=center]
  Pad40 = Pad [width=3 height=2 connect=center]
  Pad41 = Pad [width=3 height=2 connect=center]
  Pad42 = Pad [width=3 height=2 connect=center]
  Pad43 = Pad [width=3 height=2 connect=center]
  Pad44 = Pad [width=3 height=2 connect=center]
  Pad45 = Pad [width=3 height=2 connect=center]
  Pad46 = Pad [width=3 height=2 connect=center]
  Pad47 = Pad [width=3 height=2 connect=center]
  Daisy_in1 = shrouded pin header, 20 pins [form="♂ (shrouded male)"]

nets:
  N1: Pad29.pad, Daisy_in1.pin19
  N2: Pad30.pad, Daisy_in1.pin20
  N3: Pad31.pad, Daisy_in1.pin18
  N4: Pad32.pad, Daisy_in1.pin17
  N5: Pad33.pad, Daisy_in1.pin16
  N6: Pad34.pad, Daisy_in1.pin15
  N7: Pad35.pad, Daisy_in1.pin14
  N8: Pad36.pad, Daisy_in1.pin13
  N9: Pad37.pad, Daisy_in1.pin12
  N10: Pad38.pad, Daisy_in1.pin11
  N11: Pad39.pad, Daisy_in1.pin9
  N12: Pad40.pad, Daisy_in1.pin8
  N13: Pad41.pad, Daisy_in1.pin7
  N14: Pad42.pad, Daisy_in1.pin6
  N15: Pad43.pad, Daisy_in1.pin5
  N16: Pad44.pad, Daisy_in1.pin4
  N17: Pad45.pad, Daisy_in1.pin3
  N18: Pad46.pad, Daisy_in1.pin2
  N19: Pad47.pad, Daisy_in1.pin1

notes:
  WPROT
  +12V
  +5V
  -12V
  EN35
  GND
  DRV2
  PH0
  PH1
  PH2
  PH3
  WREQ
  HDSEL
  DRV1
  RD
  WR
  WRQ
  SEL
  DR1
  WPRT
  -12
  +5
  +12
  DR2
